# Fritzing sketch BCJ Indoor Environment Data Sensor (saved by Fritzing 0.9.3b)
breadboards: 1

parts:
  WeMos_D1_Mini1 = WeMos D1 Mini
  DHT1 = DHT11 Humitidy and Temperature Sensor
  DS1 = DS18B20 1-Wire Temperature Sensor [part_number=DS18B20]
  GY-1 = GY-302 [part_number=GY-302]

nets:
  3V3: WeMos_D1_Mini1.3V3, DS1.VDD, GY-1.VCC
  5V: WeMos_D1_Mini1.5V, DHT1.VDD
  N1: WeMos_D1_Mini1.A0, DS1.DQ
  N2: WeMos_D1_Mini1.D1, GY-1.SCL
  N3: WeMos_D1_Mini1.D2, GY-1.SDA
  N4: WeMos_D1_Mini1.D4, DHT1.NULL
  GND: WeMos_D1_Mini1.G, DHT1.GND, DS1.GND, GY-1.GND

notes:
  DS18B20 - gTemp Sensor
  DHT11 - Humidity Sensor
  MAX4466 - Sound Level Sensor
  IAQ air sensor breakout board, sensors can be swapped?
  BH1750 - Illuminance Sensor

custom parts:
  DHT11 Humitidy and Temperature Sensor: DHT11 Humidity and Temperature Sensor
